# Fritzing sketch Antifurto (saved by Fritzing 0.7.4b)
breadboards: 1

parts:
  Arduino1 = Arduino
  J2 = Infrared Proximity Sensor
  J3 = Infrared Proximity Sensor
  Componente1 = Arduino Cellular Shield
  Power_plug1 = Power plug
  K_GSM = Relay [part_number=FRS1B-S package=THT]
  K1 = Relay [part_number=FRS1B-S package=THT]

nets:
  GND: Arduino1.GND, J3.GND, Componente1.GND, Power_plug1.GND, K_GSM.COIL1
  N1: Arduino1.D7, J2.Vout
  N2: Arduino1.D6, J3.Vout
  N3: Arduino1.D5, K1.B
  N4: Arduino1.D4, K_GSM.COIL2
  N5: Arduino1.D3, Componente1.TX-O
  N6: Arduino1.D2, Componente1.RX-I
  VCC: Arduino1.+5V, J3.Vcc, Power_plug1.VCC, K_GSM.C1, K_GSM.C2
  N7: Componente1.5V, K_GSM.B
  N8: K1.C1, K1.C2
